# Fritzing sketch Project_2_PCB (saved by Fritzing 0.9.3b)
circuit board: 8.46667cm x 5.64444cm
breadboards: 1

parts:
  R1 = Resistor [tolerance=±5% resistance=10k package=THT]
  C1 = Ceramic Capacitor [capacitance=0.1µF voltage=5V package="100 mil [THT, multilayer]"]
  Y1 = Resonator [frequency="16 Mhz" package=THT]
  Battery = Battery block 9V
  IC2 = Voltage Regulator [package=to-92]
  C2 = Electrolytic Capacitor [capacitance=0.33µF voltage=9V package="100 mil [THT, electrolytic]"]
  C4 = Ceramic Capacitor [capacitance=0.1µF voltage=5V package="100 mil [THT, multilayer]"]
  AREF = male pin header, 1 pin [form="♂ (male)"]
  Breadboard_Power = male pin header, 2 pins [form="♂ (male)"]
  IC1 = atmega328 [package=dip]
  Header_Pins = male pin header, 20 pins [form="♂ (male)"]
  ICP = AVR ISP 6 Pin [package=2x3-ns]
  C3 = Ceramic Capacitor [capacitance=0.1µF voltage=5V package="100 mil [THT, multilayer]"]
  FTDI = male pin header, 6 pins [form="♂ (male)"]

nets:
  5V: R1.Pin_0, C1.1, IC2.OUT, Breadboard_Power.pin1, IC1.VCC, IC1.AVCC, ICP.2, C3.1, FTDI.pin3
  reset: R1.Pin_1, C4.0, IC1.RESET, ICP.5
  GND: C1.0, Y1.GND, Battery.-, IC2.GND, C2.-, Breadboard_Power.pin2, IC1.GND, ICP.6, C3.0, FTDI.pin1, FTDI.pin2
  N1: Y1.0, IC1.XLAT1
  N2: Y1.pin_1, IC1.XLAT2
  9V: Battery.+, IC2.IN, C2.+
  N3: C4.1, FTDI.pin6
  N4: AREF.pin1, IC1.AREF
  D0: IC1.D0_(RX), Header_Pins.pin7, FTDI.pin4
  D1: IC1.D1_(TX), Header_Pins.pin8, FTDI.pin5
  D2: IC1.D2, Header_Pins.pin9
  D3: IC1.D3_(PWM), Header_Pins.pin10
  D4: IC1.D4, Header_Pins.pin11
  D5: IC1.D5_(PWM), Header_Pins.pin12
  D6: IC1.D6_(PWM), Header_Pins.pin13
  D7: IC1.D7, Header_Pins.pin14
  D8: IC1.D8, Header_Pins.pin15
  D9: IC1.D9_(PWM), Header_Pins.pin16
  D10: IC1.D10_(PWM), Header_Pins.pin17
  D11: IC1.D11_(PWM), Header_Pins.pin18, ICP.4
  D12: IC1.D12, Header_Pins.pin19, ICP.1
  D13: IC1.D13, Header_Pins.pin20, ICP.3
  A0: IC1.A0, Header_Pins.pin1
  A1: IC1.A1, Header_Pins.pin2
  A2: IC1.A2, Header_Pins.pin3
  A3: IC1.A3, Header_Pins.pin4
  A4: IC1.A4, Header_Pins.pin5
  A5: IC1.A5, Header_Pins.pin6

notes:
  A0
  A5
  D0
  D4
  D5
  D8
  D9
  D13
  5V
  GND
  9V
  1
  6
